# Fritzing sketch 30_I2C LCD1602 (saved by Fritzing 0.9.3b)
breadboards: 1

parts:
  module1 = I2C LCD1602
  PART1 = Pi Wedge B+
  Raspberry_Pi_1 = Raspberry Pi 3 [part_number=RPI-3-V1.2]  # not connected

nets:
  N1: module1.SCL, module1.VCC, PART1.GPIO_3_(I2C1_SCL), PART1.5V#39, PART1.SCL, PART1.5V#71
  N2: module1.SDA, PART1.GPIO_2_(I2C1_SDA), PART1.SDA
  GND: module1.GND, PART1.GND

notes:
  I2C LCD1602

custom parts:
  I2C LCD1602: I2C LCD1602 module of ZHIYU Sensor Kit
  Pi Wedge B+: This is the Pi Wedge B Plus, a board that connects to the Raspberry Pi B+’s 40-pin GPIO connector, and breaks the pins out to breadboard-friendly arrangement and spacing, and even adds a couple of decoupling capacitors on the power supply lines. The “Wedge” also makes the initial bringup process easier - you can plug an FTDI Basic module into the built-in serial port. Each Pi Wedge comes as an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
